// Logisim project rv32i logisim.circ as structural Verilog: 9 circuits, main circuit main
module main (
  output [31:0] out_1,
  output [31:0] out_2,
  output [31:0] out_3,
  output [31:0] out_4,
  output [31:0] out_5,
  output [31:0] out_6,
  output [19:0] out_7,
  output [19:0] out_8,
  output [4:0] rs2,
  output [4:0] rs1,
  output [4:0] rd,
  output [31:0] out_12,
  output [31:0] out_13,
  output [2:0] out_14,
  output [3:0] out_15,
  output [1:0] out_16,
  output [1:0] out_17
);

  wire alu_1_compare, and_1_out, CLK_out, control_unit_1_alusrc1, control_unit_1_alusrc2,
       control_unit_1_branche, control_unit_1_jumpe, control_unit_1_load_sign_o, control_unit_1_memwrite,
       control_unit_1_regwrite, decoder_1_out0, decoder_1_out1, decoder_1_out2, not_1_out, or_1_out,
       or_2_out, R_out;
  wire [31:0] adder_1_out, adder_2_out, load_extender_1_out_val, multiplexer_1_out, multiplexer_2_out,
       register_1_q, undriven;

  Adder #(.width(32)) adder_1 (
    .a({register_1_q[31:22], out_8, register_1_q[1:0]}), .b(32'h4), .out(adder_1_out));  // open: cin, cout
  Adder #(.width(32)) adder_2 (.a(adder_1_out), .b(out_13), .out(adder_2_out));  // open: cin, cout
  Multiplexer #(.width(32)) multiplexer_1 (
    .in0(adder_1_out), .in1(adder_2_out), .out(multiplexer_1_out), .sel(and_1_out));
  not not_1 (not_1_out, CLK_out);
  Register #(.width(32)) register_1 (
    .D(multiplexer_2_out), .en(1'b1), .clk(not_1_out), .Q({register_1_q[31:22], out_8, register_1_q[1:0]}),
    .clr(R_out));
  Multiplexer #(.width(32)) multiplexer_2 (
    .in0(multiplexer_1_out), .in1(out_4), .out(multiplexer_2_out), .sel(control_unit_1_jumpe));
  RAM #(.addrWidth(20), .asyncread("true"), .dataWidth(32)) Instruction_mem (
    .addr(out_8), .we(1'b0), .oe(1'b1), .dout(out_6));  // open: clk, din
  Clock CLK (.out(CLK_out));
  Button R (.out(R_out));
  Control_Unit control_unit_1 (
    .Funct7(out_6[31:25]), .Funct3(out_6[14:12]), .Opcode(out_6[6:0]), .RegWrite(control_unit_1_regwrite),
    .Format(out_14), .ALUsrc1(control_unit_1_alusrc1), .ALUsrc2(control_unit_1_alusrc2), .Op(out_15),
    .JumpE(control_unit_1_jumpe), .rd_source(out_16), .BranchE(control_unit_1_branche),
    .MemWrite(control_unit_1_memwrite), .Mem_Data_size(out_17), .Load_sign_o(control_unit_1_load_sign_o));
  Multiplexer #(.select(2), .width(32)) multiplexer_3 (
    .in0(out_4), .in1(load_extender_1_out_val), .in2(out_13), .in3(adder_1_out), .out(out_2), .sel(out_16));
  and and_1 (and_1_out, control_unit_1_branche, alu_1_compare);
  Imm_Gen imm_gen_1 (.Imm_In(out_6[31:6]), .Format(out_14), .Imm_extended(out_13));
  Register_File register_file_1 (
    .Write_data(out_2), .RegWrite(control_unit_1_regwrite), .Clock(CLK_out), .rs2(out_6[24:20]),
    .rd(out_6[11:7]), .rs1(out_6[19:15]), .Reset(R_out), .Reg1(out_1), .Reg2(out_12));
  Multiplexer #(.width(32)) multiplexer_4 (.in0(out_1), .in1(adder_1_out), .out(out_3), .sel(control_unit_1_alusrc1));
  Multiplexer #(.width(32)) multiplexer_5 (.in0(out_12), .in1(out_13), .out(out_5), .sel(control_unit_1_alusrc2));
  ALU alu_1 (.InputA(out_3), .InputB(out_5), .Op(out_15), .Result(out_4), .Compare(alu_1_compare));
  Decoder #(.select(2)) decoder_1 (
    .out0(decoder_1_out0), .out1(decoder_1_out1), .out2(decoder_1_out2), .sel(out_17), .en(1'b1));  // open: out3
  or or_1 (or_1_out, decoder_1_out0, decoder_1_out1);
  RAM #(.addrWidth(20), .byteenables("byteEnables"), .dataWidth(32)) Data_mem (
    .addr(out_4[21:2]), .we(control_unit_1_memwrite), .oe(1'b1), .clk(CLK_out), .din(out_12),
    .be3(decoder_1_out0), .be2(decoder_1_out0), .be1(or_1_out), .be0(or_2_out));  // open: dout
  or or_2 (or_2_out, or_1_out, decoder_1_out2);
  Load_extender load_extender_1 (
    .In_Val(undriven), .Size(out_17), .Sign(control_unit_1_load_sign_o), .Out_Val(load_extender_1_out_val));

  assign out_7 = out_4[21:2];
  assign rd = out_6[11:7];
  assign rs1 = out_6[19:15];
  assign rs2 = out_6[24:20];
endmodule

module Register_File (
  input  [31:0] Write_data,
  input  RegWrite,
  input  Clock,
  input  [4:0] rs2,
  input  [4:0] rd,
  input  [4:0] rs1,
  input  Reset,
  output [31:0] Reg1,
  output [31:0] Reg2
);

  wire and_1_out, decoder_1_out1, decoder_1_out2, decoder_1_out3, decoder_1_out4, decoder_1_out5,
       decoder_1_out6, decoder_1_out7, decoder_1_out8, decoder_1_out9, decoder_1_out10, decoder_1_out11,
       decoder_1_out12, decoder_1_out13, decoder_1_out14, decoder_1_out15, decoder_1_out16, decoder_1_out17,
       decoder_1_out18, decoder_1_out19, decoder_1_out20, decoder_1_out21, decoder_1_out22, decoder_1_out23,
       decoder_1_out24, decoder_1_out25, decoder_1_out26, decoder_1_out27, decoder_1_out28, decoder_1_out29,
       decoder_1_out30, decoder_1_out31;
  wire [31:0] register_1_q, register_2_q, register_3_q, register_4_q, register_5_q, register_6_q,
       register_7_q, register_8_q, register_9_q, register_10_q, register_11_q, register_12_q, register_13_q,
       register_14_q, register_15_q, register_16_q, register_17_q, register_18_q, register_19_q,
       register_20_q, register_21_q, register_22_q, register_23_q, register_24_q, register_25_q,
       register_26_q, register_27_q, register_28_q, register_29_q, register_30_q, register_31_q;

  Decoder #(.select(5)) decoder_1 (
    .out1(decoder_1_out1), .out2(decoder_1_out2), .out3(decoder_1_out3), .out4(decoder_1_out4),
    .out5(decoder_1_out5), .out6(decoder_1_out6), .out7(decoder_1_out7), .out8(decoder_1_out8),
    .out9(decoder_1_out9), .out10(decoder_1_out10), .out11(decoder_1_out11), .out12(decoder_1_out12),
    .out13(decoder_1_out13), .out14(decoder_1_out14), .out15(decoder_1_out15), .out16(decoder_1_out16),
    .out17(decoder_1_out17), .out18(decoder_1_out18), .out19(decoder_1_out19), .out20(decoder_1_out20),
    .out21(decoder_1_out21), .out22(decoder_1_out22), .out23(decoder_1_out23), .out24(decoder_1_out24),
    .out25(decoder_1_out25), .out26(decoder_1_out26), .out27(decoder_1_out27), .out28(decoder_1_out28),
    .out29(decoder_1_out29), .out30(decoder_1_out30), .out31(decoder_1_out31), .sel(rd), .en(1'b1));  // open: out0
  and and_1 (and_1_out, RegWrite, Clock);
  Register #(.width(32)) register_1 (
    .D(Write_data), .en(decoder_1_out2), .clk(and_1_out), .Q(register_1_q), .clr(Reset));
  Register #(.width(32)) register_2 (
    .D(Write_data), .en(decoder_1_out4), .clk(and_1_out), .Q(register_2_q), .clr(Reset));
  Register #(.width(32)) register_3 (
    .D(Write_data), .en(decoder_1_out6), .clk(and_1_out), .Q(register_3_q), .clr(Reset));
  Register #(.width(32)) register_4 (
    .D(Write_data), .en(decoder_1_out8), .clk(and_1_out), .Q(register_4_q), .clr(Reset));
  Register #(.width(32)) register_5 (
    .D(Write_data), .en(decoder_1_out10), .clk(and_1_out), .Q(register_5_q), .clr(Reset));
  Register #(.width(32)) register_6 (
    .D(Write_data), .en(decoder_1_out12), .clk(and_1_out), .Q(register_6_q), .clr(Reset));
  Register #(.width(32)) register_7 (
    .D(Write_data), .en(decoder_1_out14), .clk(and_1_out), .Q(register_7_q), .clr(Reset));
  Register #(.width(32)) register_8 (
    .D(Write_data), .en(decoder_1_out16), .clk(and_1_out), .Q(register_8_q), .clr(Reset));
  Register #(.width(32)) register_9 (
    .D(Write_data), .en(decoder_1_out18), .clk(and_1_out), .Q(register_9_q), .clr(Reset));
  Register #(.width(32)) register_10 (
    .D(Write_data), .en(decoder_1_out20), .clk(and_1_out), .Q(register_10_q), .clr(Reset));
  Register #(.width(32)) register_11 (
    .D(Write_data), .en(decoder_1_out22), .clk(and_1_out), .Q(register_11_q), .clr(Reset));
  Register #(.width(32)) register_12 (
    .D(Write_data), .en(decoder_1_out24), .clk(and_1_out), .Q(register_12_q), .clr(Reset));
  Register #(.width(32)) register_13 (
    .D(Write_data), .en(decoder_1_out26), .clk(and_1_out), .Q(register_13_q), .clr(Reset));
  Register #(.width(32)) register_14 (
    .D(Write_data), .en(decoder_1_out28), .clk(and_1_out), .Q(register_14_q), .clr(Reset));
  Register #(.width(32)) register_15 (
    .D(Write_data), .en(decoder_1_out30), .clk(and_1_out), .Q(register_15_q), .clr(Reset));
  Register #(.width(32)) register_16 (
    .D(Write_data), .en(decoder_1_out1), .clk(and_1_out), .Q(register_16_q), .clr(Reset));
  Register #(.width(32)) register_17 (
    .D(Write_data), .en(decoder_1_out3), .clk(and_1_out), .Q(register_17_q), .clr(Reset));
  Register #(.width(32)) register_18 (
    .D(Write_data), .en(decoder_1_out5), .clk(and_1_out), .Q(register_18_q), .clr(Reset));
  Register #(.width(32)) register_19 (
    .D(Write_data), .en(decoder_1_out7), .clk(and_1_out), .Q(register_19_q), .clr(Reset));
  Register #(.width(32)) register_20 (
    .D(Write_data), .en(decoder_1_out9), .clk(and_1_out), .Q(register_20_q), .clr(Reset));
  Register #(.width(32)) register_21 (
    .D(Write_data), .en(decoder_1_out11), .clk(and_1_out), .Q(register_21_q), .clr(Reset));
  Register #(.width(32)) register_22 (
    .D(Write_data), .en(decoder_1_out13), .clk(and_1_out), .Q(register_22_q), .clr(Reset));
  Register #(.width(32)) register_23 (
    .D(Write_data), .en(decoder_1_out15), .clk(and_1_out), .Q(register_23_q), .clr(Reset));
  Register #(.width(32)) register_24 (
    .D(Write_data), .en(decoder_1_out17), .clk(and_1_out), .Q(register_24_q), .clr(Reset));
  Register #(.width(32)) register_25 (
    .D(Write_data), .en(decoder_1_out19), .clk(and_1_out), .Q(register_25_q), .clr(Reset));
  Register #(.width(32)) register_26 (
    .D(Write_data), .en(decoder_1_out21), .clk(and_1_out), .Q(register_26_q), .clr(Reset));
  Register #(.width(32)) register_27 (
    .D(Write_data), .en(decoder_1_out23), .clk(and_1_out), .Q(register_27_q), .clr(Reset));
  Register #(.width(32)) register_28 (
    .D(Write_data), .en(decoder_1_out25), .clk(and_1_out), .Q(register_28_q), .clr(Reset));
  Register #(.width(32)) register_29 (
    .D(Write_data), .en(decoder_1_out27), .clk(and_1_out), .Q(register_29_q), .clr(Reset));
  Register #(.width(32)) register_30 (
    .D(Write_data), .en(decoder_1_out29), .clk(and_1_out), .Q(register_30_q), .clr(Reset));
  Register #(.width(32)) register_31 (
    .D(Write_data), .en(decoder_1_out31), .clk(and_1_out), .Q(register_31_q), .clr(Reset));
  Multiplexer #(.enable("true"), .select(5), .width(32)) multiplexer_1 (
    .in0({32{1'b0}}), .in1(register_16_q), .in2(register_1_q), .in3(register_17_q), .in4(register_2_q),
    .in5(register_18_q), .in6(register_3_q), .in7(register_19_q), .in8(register_4_q), .in9(register_20_q),
    .in10(register_5_q), .in11(register_21_q), .in12(register_6_q), .in13(register_22_q),
    .in14(register_7_q), .in15(register_23_q), .in16(register_8_q), .in17(register_24_q),
    .in18(register_9_q), .in19(register_25_q), .in20(register_10_q), .in21(register_26_q),
    .in22(register_11_q), .in23(register_27_q), .in24(register_12_q), .in25(register_28_q),
    .in26(register_13_q), .in27(register_29_q), .in28(register_14_q), .in29(register_30_q),
    .in30(register_15_q), .in31(register_31_q), .out(Reg2), .sel(rs2), .en(1'b1));
  Multiplexer #(.enable("true"), .select(5), .width(32)) multiplexer_2 (
    .in0({32{1'b0}}), .in1(register_16_q), .in2(register_1_q), .in3(register_17_q), .in4(register_2_q),
    .in5(register_18_q), .in6(register_3_q), .in7(register_19_q), .in8(register_4_q), .in9(register_20_q),
    .in10(register_5_q), .in11(register_21_q), .in12(register_6_q), .in13(register_22_q),
    .in14(register_7_q), .in15(register_23_q), .in16(register_8_q), .in17(register_24_q),
    .in18(register_9_q), .in19(register_25_q), .in20(register_10_q), .in21(register_26_q),
    .in22(register_11_q), .in23(register_27_q), .in24(register_12_q), .in25(register_28_q),
    .in26(register_13_q), .in27(register_29_q), .in28(register_14_q), .in29(register_30_q),
    .in30(register_15_q), .in31(register_31_q), .out(Reg1), .sel(rs1), .en(1'b1));
endmodule

module PC (
  input  BranchE,
  input  [31:0] Branch_Address,
  input  JumpE,
  input  Clock,
  input  [31:0] Jump_Address,
  input  Reset,
  output [31:0] PC_reg
);

  wire [31:0] adder_1_out, adder_2_out, multiplexer_1_out, multiplexer_2_out, shifter_1_out;

  Adder #(.width(32)) adder_1 (.a(PC_reg), .b(32'h4), .out(adder_1_out));  // open: cin, cout
  Shifter #(.width(32)) shifter_1 (.in(Branch_Address), .\dist (5'b00010), .out(shifter_1_out));
  Adder #(.width(32)) adder_2 (.a(adder_1_out), .b(shifter_1_out), .out(adder_2_out));  // open: cin, cout
  Multiplexer #(.width(32)) multiplexer_1 (
    .in0(adder_1_out), .in1(adder_2_out), .out(multiplexer_1_out), .sel(BranchE));
  Multiplexer #(.width(32)) multiplexer_2 (
    .in0(multiplexer_1_out), .in1(Jump_Address), .out(multiplexer_2_out), .sel(JumpE));
  Register #(.width(32)) register_1 (.D(multiplexer_2_out), .en(1'b1), .clk(Clock), .Q(PC_reg), .clr(Reset));
endmodule

module Imm_Gen (
  input  [25:0] Imm_In,
  input  [2:0] Format,
  output [31:0] Imm_extended
);

  wire [31:0] bit_extender_1_out, bit_extender_2_out, bit_extender_3_out, bit_extender_4_out;

  assign bit_extender_1_out = {{20{Imm_In[25]}}, {Imm_In[25:19], Imm_In[4:0]}};  // Bit_Extender bit_extender_1
  assign bit_extender_2_out = {{19{Imm_In[25]}}, {Imm_In[25], Imm_In[0], Imm_In[24:19], Imm_In[4:1], 1'b0}};  // Bit_Extender bit_extender_2
  assign bit_extender_3_out = {{11{Imm_In[25]}}, {Imm_In[25], Imm_In[13:6], Imm_In[14], Imm_In[24:15], 1'b0}};  // Bit_Extender bit_extender_3
  assign bit_extender_4_out = {{20{Imm_In[25]}}, Imm_In[25:14]};  // Bit_Extender bit_extender_4
  Multiplexer #(.select(3), .width(32)) multiplexer_1 (
    .in0(bit_extender_4_out), .in1(bit_extender_1_out), .in2(bit_extender_2_out),
    .in3({Imm_In[25:6], {12{1'b0}}}), .in4(bit_extender_3_out), .out(Imm_extended), .sel(Format));  // open: in5, in6, in7

  // Notes on the sheet:
  //   I-Format
  //   S-Format
  //   B-Format
  //   U-Format
  //   J-Format
endmodule

module ALU (
  input  [31:0] InputA,
  input  [31:0] InputB,
  input  [3:0] Op,
  output [31:0] Result,
  output Compare
);

  wire comparator_1_gt, comparator_1_lt, comparator_2_eq, comparator_2_gt, comparator_2_lt, not_1_out,
       or_2_out, or_3_out;
  wire [31:0] adder_1_out, and_1_out, bit_extender_1_out, bit_extender_2_out, bit_extender_3_out,
       bit_extender_4_out, bit_extender_5_out, bit_extender_6_out, bit_extender_7_out, bit_extender_8_out,
       or_1_out, shifter_1_out, shifter_2_out, shifter_3_out, subtractor_1_out, xor_1_out;

  Adder #(.width(32)) adder_1 (.a(InputA), .b(InputB), .out(adder_1_out));  // open: cin, cout
  Subtractor #(.width(32)) subtractor_1 (.a(InputA), .b(InputB), .out(subtractor_1_out));  // open: bin, bout
  Shifter #(.width(32)) shifter_1 (.in(InputA), .\dist (InputB[4:0]), .out(shifter_1_out));
  Shifter #(.shift("lr"), .width(32)) shifter_2 (.in(InputA), .\dist (InputB[4:0]), .out(shifter_2_out));
  Shifter #(.shift("ar"), .width(32)) shifter_3 (.in(InputA), .\dist (InputB[4:0]), .out(shifter_3_out));
  assign xor_1_out = InputA ^ InputB;  // XOR_Gate xor_1, 32 bits wide
  assign and_1_out = InputA & InputB;  // AND_Gate and_1, 32 bits wide
  assign or_1_out = InputA | InputB;  // OR_Gate or_1, 32 bits wide
  Comparator #(.width(32)) comparator_1 (
    .a(InputA), .b(InputB), .gt(comparator_1_gt), .lt(comparator_1_lt));  // open: eq
  Comparator #(.mode("unsigned"), .width(32)) comparator_2 (
    .a(InputA), .b(InputB), .gt(comparator_2_gt), .eq(comparator_2_eq), .lt(comparator_2_lt));
  not not_1 (not_1_out, comparator_2_eq);
  or or_2 (or_2_out, comparator_2_eq, comparator_1_gt);
  or or_3 (or_3_out, comparator_2_eq, comparator_2_gt);
  assign bit_extender_1_out = {{31{1'b0}}, comparator_1_lt};  // Bit_Extender bit_extender_1
  assign bit_extender_2_out = {{31{1'b0}}, comparator_2_lt};  // Bit_Extender bit_extender_2
  assign bit_extender_3_out = {{31{1'b0}}, comparator_2_eq};  // Bit_Extender bit_extender_3
  assign bit_extender_4_out = {{31{1'b0}}, not_1_out};  // Bit_Extender bit_extender_4
  assign bit_extender_5_out = {{31{1'b0}}, comparator_1_lt};  // Bit_Extender bit_extender_5
  assign bit_extender_6_out = {{31{1'b0}}, or_2_out};  // Bit_Extender bit_extender_6
  assign bit_extender_7_out = {{31{1'b0}}, comparator_2_lt};  // Bit_Extender bit_extender_7
  assign bit_extender_8_out = {{31{1'b0}}, or_3_out};  // Bit_Extender bit_extender_8
  Multiplexer #(.select(4), .width(32)) multiplexer_1 (
    .in0(adder_1_out), .in1(subtractor_1_out), .in2(shifter_1_out), .in3(shifter_2_out), .in4(shifter_3_out),
    .in5(xor_1_out), .in6(and_1_out), .in7(or_1_out), .in8(bit_extender_1_out), .in9(bit_extender_2_out),
    .in10(bit_extender_3_out), .in11(bit_extender_4_out), .in12(bit_extender_5_out),
    .in13(bit_extender_6_out), .in14(bit_extender_7_out), .in15(bit_extender_8_out),
    .out({Result[31:1], Compare}), .sel(Op));

  assign Result[0] = Compare;

  // Notes on the sheet:
  //   slt
  //   sltu
  //   eq
  //   ne
  //   lt
  //   ge
  //   ltu
  //   geu
endmodule

module OpcodeToFormat (
  input  [6:0] OpCode,
  output R_format,
  output I1_format,
  output I2_format,
  output jalr,
  output S_format,
  output B_format,
  output jal,
  output lui,
  output auipc
);

  Decoder #(.select(5)) decoder_1 (
    .out0(I2_format), .out3(auipc), .out4(I1_format), .out8(S_format), .out12(R_format), .out13(lui),
    .out24(B_format), .out25(jalr), .out27(jal), .sel(OpCode[6:2]), .en(1'b1));  // open: out1, out2, out5, out6, out7, out9, out10, out11, out14, out15, out16, out17, out18, out19, out20, out21, out22, out23, out26, out28, out29, out30, out31

  // Notes on the sheet:
  //   B-format
endmodule

module Control_Unit (
  input  [6:0] Funct7,
  input  [2:0] Funct3,
  input  [6:0] Opcode,
  output RegWrite,
  output [2:0] Format,
  output ALUsrc1,
  output ALUsrc2,
  output [3:0] Op,
  output JumpE,
  output [1:0] rd_source,
  output BranchE,
  output MemWrite,
  output [1:0] Mem_Data_size,
  output Load_sign_o
);

  wire and_1_out, and_4_out, and_5_out, and_6_out, and_7_out, and_8_out, and_9_out, and_10_out, and_11_out,
       and_12_out, and_13_out, and_14_out, and_15_out, and_16_out, and_17_out, and_18_out, and_19_out,
       and_20_out, and_21_out, and_22_out, and_23_out, and_24_out, and_25_out, and_26_out, and_27_out,
       and_28_out, and_29_out, and_30_out, and_31_out, and_32_out, and_33_out, decoder_1_out0,
       decoder_1_out1, decoder_1_out2, decoder_1_out3, decoder_1_out4, decoder_1_out5, decoder_1_out6,
       decoder_1_out7, decoder_2_out0, decoder_2_out1, decoder_3_out0, decoder_3_out1, decoder_4_out0,
       decoder_4_out1, opcodetoformat_1_b_format, opcodetoformat_1_i1_format, opcodetoformat_1_i2_format,
       opcodetoformat_1_jal, opcodetoformat_1_jalr, opcodetoformat_1_r_format, opcodetoformat_1_s_format,
       or_1_out, or_3_out, or_4_out, or_5_out, or_7_out, or_8_out, or_9_out, or_10_out, or_11_out, or_12_out,
       or_13_out, or_14_out, or_15_out, or_16_out, or_17_out, or_18_out, or_19_out, or_21_out,
       priority_encoder_1_p4, priority_encoder_1_p5, priority_encoder_4_gs;

  and and_1 (and_1_out, Opcode[0], Opcode[1]);
  and and_2 (JumpE, and_1_out, or_1_out);
  Decoder #(.select(3)) decoder_1 (
    .out0(decoder_1_out0), .out1(decoder_1_out1), .out2(decoder_1_out2), .out3(decoder_1_out3),
    .out4(decoder_1_out4), .out5(decoder_1_out5), .out6(decoder_1_out6), .out7(decoder_1_out7), .sel(Funct3),
    .en(1'b1));
  or or_1 (or_1_out, opcodetoformat_1_jal, opcodetoformat_1_jalr);
  // Priority_Encoder #(.select(2)) priority_encoder_1: pin names not known; wires that end beside it: 1'b1, or_1_out, rd_source, priority_encoder_1_p4, priority_encoder_1_p5, 1'b1
  or or_2 (ALUsrc2, opcodetoformat_1_i1_format, opcodetoformat_1_i2_format, opcodetoformat_1_jalr, opcodetoformat_1_s_format);
  OpcodeToFormat opcodetoformat_1 (
    .OpCode(Opcode), .R_format(opcodetoformat_1_r_format), .I1_format(opcodetoformat_1_i1_format),
    .I2_format(opcodetoformat_1_i2_format), .jalr(opcodetoformat_1_jalr),
    .S_format(opcodetoformat_1_s_format), .B_format(opcodetoformat_1_b_format), .jal(opcodetoformat_1_jal),
    .lui(priority_encoder_1_p4), .auipc(ALUsrc1));
  or or_3 (or_3_out, opcodetoformat_1_i1_format, opcodetoformat_1_i2_format, opcodetoformat_1_jalr);
  or or_4 (or_4_out, ALUsrc1, priority_encoder_1_p4);
  or or_5 (or_5_out, or_3_out, or_4_out, opcodetoformat_1_jal);
  Priority_Encoder priority_encoder_2 (
    .in0(or_3_out), .in1(opcodetoformat_1_s_format), .in2(opcodetoformat_1_b_format), .in3(or_4_out),
    .in4(opcodetoformat_1_jal), .out(Format), .en_in(1'b1));  // open: in5, in6, in7, gs, en_out
  and and_3 (RegWrite, and_1_out, or_5_out);
  and and_4 (and_4_out, opcodetoformat_1_r_format, decoder_1_out0);
  and and_5 (and_5_out, opcodetoformat_1_r_format, decoder_1_out5);
  and and_6 (and_6_out, opcodetoformat_1_r_format, decoder_1_out1);
  and and_7 (and_7_out, opcodetoformat_1_r_format, decoder_1_out6);
  and and_8 (and_8_out, opcodetoformat_1_r_format, decoder_1_out4);
  and and_9 (and_9_out, opcodetoformat_1_r_format, decoder_1_out7);
  and and_10 (and_10_out, opcodetoformat_1_r_format, decoder_1_out2);
  and and_11 (and_11_out, opcodetoformat_1_r_format, decoder_1_out3);
  and and_12 (and_12_out, opcodetoformat_1_i1_format, decoder_1_out0);
  and and_13 (and_13_out, opcodetoformat_1_i1_format, decoder_1_out3);
  and and_14 (and_14_out, opcodetoformat_1_i1_format, decoder_1_out5);
  and and_15 (and_15_out, opcodetoformat_1_i1_format, decoder_1_out6);
  and and_16 (and_16_out, opcodetoformat_1_i1_format, decoder_1_out1);
  and and_17 (and_17_out, opcodetoformat_1_i1_format, decoder_1_out5);
  and and_18 (and_18_out, opcodetoformat_1_i1_format, decoder_1_out2);
  and and_19 (and_19_out, opcodetoformat_1_i1_format, decoder_1_out3);
  and and_20 (and_20_out, opcodetoformat_1_b_format, decoder_1_out0);
  and and_21 (and_21_out, opcodetoformat_1_b_format, decoder_1_out1);
  and and_22 (and_22_out, opcodetoformat_1_b_format, decoder_1_out4);
  and and_23 (and_23_out, opcodetoformat_1_b_format, decoder_1_out5);
  and and_24 (and_24_out, opcodetoformat_1_b_format, decoder_1_out6);
  and and_25 (and_25_out, opcodetoformat_1_b_format, decoder_1_out7);
  and and_26 (and_26_out, opcodetoformat_1_s_format, decoder_1_out0);
  and and_27 (and_27_out, opcodetoformat_1_s_format, decoder_1_out1);
  and and_28 (and_28_out, opcodetoformat_1_s_format, decoder_1_out2);
  and and_29 (and_29_out, opcodetoformat_1_i2_format, decoder_1_out0);
  and and_30 (and_30_out, opcodetoformat_1_i2_format, decoder_1_out1);
  and and_31 (and_31_out, opcodetoformat_1_i2_format, decoder_1_out2);
  and and_32 (and_32_out, opcodetoformat_1_i2_format, decoder_1_out4);
  and and_33 (and_33_out, opcodetoformat_1_i2_format, decoder_1_out5);
  Decoder decoder_2 (.out0(decoder_2_out0), .out1(decoder_2_out1), .sel(Funct7[5]), .en(and_4_out));
  Decoder decoder_3 (.out0(decoder_3_out0), .out1(decoder_3_out1), .sel(Funct7[5]), .en(and_5_out));
  Decoder decoder_4 (.out0(decoder_4_out0), .out1(decoder_4_out1), .sel(Funct7[5]), .en(and_17_out));
  or or_6 (priority_encoder_1_p5, and_33_out, and_32_out, and_31_out, and_30_out, and_29_out);
  or or_7 (or_7_out, and_26_out, and_27_out, and_28_out);
  or or_8 (or_8_out, opcodetoformat_1_jalr, decoder_2_out0, and_12_out);
  or or_9 (or_9_out, and_8_out, and_13_out);
  or or_10 (or_10_out, and_7_out, and_14_out);
  or or_11 (or_11_out, and_9_out, and_15_out);
  or or_12 (or_12_out, and_6_out, and_16_out);
  or or_13 (or_13_out, decoder_3_out0, decoder_4_out0);
  or or_14 (or_14_out, decoder_3_out1, decoder_4_out1);
  or or_15 (or_15_out, and_10_out, and_18_out);
  or or_16 (or_16_out, and_11_out, and_19_out);
  or or_17 (or_17_out, and_28_out, and_31_out);
  or or_18 (or_18_out, and_27_out, and_30_out, and_33_out);
  or or_19 (or_19_out, and_26_out, and_29_out, and_32_out);
  or or_20 (Load_sign_o, and_32_out, and_33_out);
  Priority_Encoder #(.select(2)) priority_encoder_3 (
    .in0(or_17_out), .in1(or_18_out), .in2(or_19_out), .in3(1'b0), .out(Mem_Data_size), .en_in(1'b1));  // open: gs, en_out
  Priority_Encoder #(.select(4)) priority_encoder_4 (
    .in0(or_8_out), .in1(decoder_2_out1), .in2(or_9_out), .in3(or_10_out), .in4(or_11_out), .in5(or_12_out),
    .in6(or_13_out), .in7(or_14_out), .in8(or_15_out), .in9(or_16_out), .in10(and_20_out), .in11(and_21_out),
    .in12(and_22_out), .in13(and_23_out), .in14(and_24_out), .in15(and_25_out), .out(Op),
    .gs(priority_encoder_4_gs), .en_in(1'b1));  // open: en_out
  or or_21 (or_21_out, and_20_out, and_21_out, and_22_out, and_23_out, and_24_out, and_25_out);
  and and_34 (BranchE, or_21_out, and_1_out);
  and and_35 (MemWrite, or_7_out, and_1_out);

  // Notes on the sheet:
  //   add
  //   srl
  //   sra
  //   sll
  //   or
  //   xor
  //   and
  //   slt
  //   sltu
  //   addi
  //   xori
  //   ori
  //   andi
  //   slli
  //   srli
  //   slti
  //   sltiu
  //   beq
  //   bne
  //   blt
  //   bge
  //   bltu
  //   bgeu
  //   sb
  //   sh
  //   sw
  //   lb
  //   lh
  //   lw
  //   lbu
  //   lhu
  //   sub
  //   srai
endmodule

module Store_extender (
  input  [31:0] In_Val,
  input  [1:0] Store_Size,
  input  [31:0] Prev_Data,
  output [31:0] Out_Val
);

  Multiplexer #(.select(2), .width(32)) multiplexer_1 (
    .in0(In_Val), .in1({Prev_Data[31:16], In_Val[15:0]}), .in2({Prev_Data[31:8], In_Val[7:0]}),
    .out(Out_Val), .sel(Store_Size));  // open: in3

  // Notes on the sheet:
  //   Store_Size
endmodule

module Load_extender (
  input  [31:0] In_Val,
  input  [1:0] Size,
  input  Sign,
  output [31:0] Out_Val
);

  wire [31:0] bit_extender_1_out, bit_extender_2_out, bit_extender_3_out, bit_extender_4_out,
       multiplexer_1_out, multiplexer_2_out;

  assign bit_extender_1_out = {{16{1'b0}}, In_Val[15:0]};  // Bit_Extender bit_extender_1
  assign bit_extender_2_out = {{16{In_Val[15]}}, In_Val[15:0]};  // Bit_Extender bit_extender_2
  assign bit_extender_3_out = {{24{1'b0}}, In_Val[7:0]};  // Bit_Extender bit_extender_3
  assign bit_extender_4_out = {{24{In_Val[7]}}, In_Val[7:0]};  // Bit_Extender bit_extender_4
  Multiplexer #(.width(32)) multiplexer_1 (
    .in0(bit_extender_1_out), .in1(bit_extender_2_out), .out(multiplexer_1_out), .sel(Sign));
  Multiplexer #(.width(32)) multiplexer_2 (
    .in0(bit_extender_3_out), .in1(bit_extender_4_out), .out(multiplexer_2_out), .sel(Sign));
  Multiplexer #(.select(2), .width(32)) multiplexer_3 (
    .in0(In_Val), .in1(multiplexer_1_out), .in2(multiplexer_2_out), .out(Out_Val), .sel(Size));  // open: in3
endmodule
